# Fritzing sketch SKETCH_LKTI (saved by Fritzing 0.9.3b)

parts:
  o1 = Module display OLED I2C 128x64 SSD1306 [package=THT]
  Part1 = Arduino Nano (Rev3.0)
  DFRobot_DFPlayer_Mini1 = DFRobot DFPlayer Mini [part_number=DFR0299]
  AMP1 = GF1002 Stereo Amplifier
  SEN1 = Pulse Sensor [package=SIP]
  BAT1 = Battery Holders [package=lipo-1100mAh]
  SP4 = SPEAKER [package=pcb_mount_speaker]
  SP5 = SPEAKER [package=pcb_mount_speaker]
  MOTOR1 = Vibration Motor
  MOTOR2 = Vibration Motor

nets:
  GND: o1.GND, Part1.GND, MOTOR2.NEG
  VCC: o1.VCC, Part1.5V, DFRobot_DFPlayer_Mini1.VCC
  N1: o1.SCL, Part1.A5
  N2: o1.SDA, Part1.A4
  N3: Part1.D1/TX, DFRobot_DFPlayer_Mini1.RX
  N4: Part1.D0/RX, DFRobot_DFPlayer_Mini1.TX
  N5: Part1.D3, SEN1.Signal
  N6: Part1.D4, MOTOR1.POS
  N7: Part1.D5, MOTOR2.POS
  N8: DFRobot_DFPlayer_Mini1.DAC_R, AMP1.INPUTL
  N9: DFRobot_DFPlayer_Mini1.DAC_L, AMP1.INPUTR
  N10: DFRobot_DFPlayer_Mini1.GND-1, DFRobot_DFPlayer_Mini1.GND-2, AMP1.INPUTG
  N11: AMP1.ROUT-, SP5.+
  N12: AMP1.ROUT+, SP5.-
  N13: AMP1.LOUT+, SP4.-
  N14: AMP1.LOUT-, SP4.+
  N15: AMP1.POWER-, BAT1.-
  N16: AMP1.POWER+, BAT1.+

custom parts:
  Module display OLED I2C 128x64 SSD1306: Ecran OLED I2C SSD163 de 128x64 avec connexion I2C
  GF1002 Stereo Amplifier: GF1002 6 Watt Stereo Amplifier
  Pulse Sensor: Pulse Sensor Optical Heart Rate Monitor for Arduino and other microcontrollers
  Vibration Motor: An eccentric vibration motor!
